# Fritzing sketch countdown (saved by Fritzing 0.9.3b)
circuit board: 8.46667cm x 5.64444cm
breadboards: 1

parts:
  U1 = SO16 [chip_label=TLC5916 package=SO]  # not connected
  7_Segment1 = 7 Segment Display  # not connected
  U3 = IC, SIP package, 5 pins [chip_label=IC]
  U4 = SO16 [chip_label=TLC5916 package=SO]
  U2 = IC, SIP package, 5 pins [chip_label=IC]

nets:
  N1: U3.pin1, U4.6
  N2: U3.pin2, U4.7
  N3: U3.pin4, U4.8
  N4: U3.pin5, U4.9
  N5: U4.5, U2.pin5
  N6: U4.10, U2.pin1
  N7: U4.11, U2.pin2
  N8: U4.12, U2.pin4
